// Digital circuit Ping_Pong.dig as structural Verilog
module Ping_Pong (
  input  clk
);

  wire _74193_1_p8, _744017_1_p3, and_1_out, delay_1_out, diodeforward_1_out, pulldown_1_out;
  wire [2:0] _74193_1_p13;
  wire [3:0] _744017_1_p8;

  PullDown pulldown_1 (.out(pulldown_1_out));
  assign pulldown_1_out = ~_744017_1_p8[3] ? delay_1_out : 1'bz;  // DriverInvSel driverinvsel_1
  DiodeForward diodeforward_1 (.in(pulldown_1_out), .out(diodeforward_1_out));
  PullDown pulldown_2 (.out(diodeforward_1_out));
  assign diodeforward_1_out = ~pulldown_1_out ? clk : 1'bz;  // DriverInvSel driverinvsel_2
  Delay delay_1 (.in(_744017_1_p8[3]), .out(delay_1_out));
  // _74193 _74193_1: pin names not known; wires that end beside it: clk, 1'b1, diodeforward_1_out, 1'b0, 1'b0, 1'b0, 1'b0, _74193_1_p8, 1'b1, 1'b1, 1'b0, _74193_1_p13[0], _74193_1_p13[1], _74193_1_p13[2]
  // _744017 _744017_1: pin names not known; wires that end beside it: 1'b0, clk, _744017_1_p3, 1'b1, 1'b0, _744017_1_p8[0], _744017_1_p8[1], _744017_1_p8[2], _744017_1_p8[3], _744017_1_p3
  and and_1 (and_1_out, _74193_1_p13[2], _74193_1_p13[2]);
  assign _74193_1_p8 = _744017_1_p8[3] ? _744017_1_p8[3] : 1'bz;  // Driver driver_1
  PullDown pulldown_3 (.out(_74193_1_p8));
  LedMatrix #(.rowDataBits(4)) ledmatrix_1 (.rows(_744017_1_p8), .column(_74193_1_p13));
  assign _74193_1_p8 = ~_74193_1_p8 ? and_1_out : 1'bz;  // DriverInvSel driverinvsel_3

  // Notes on the sheet:
  //   clk: Hz: 20
endmodule
