// Digital circuit Ping_Pongv2.dig as structural Verilog
module Ping_Pongv2 (
  input  clk
);

  wire _74138_1_p9, _74138_1_p10, _74138_1_p11, _74138_1_p12, _74138_1_p13, _74138_1_p14, _74138_1_p15,
       _74138_1_p16, _74138_2_p9, _74138_2_p10, _74138_2_p11, _74138_2_p12, _74138_2_p13, _74138_2_p14,
       _74138_2_p15, _74138_2_p16, _74175_1_p5, _74175_1_p9, _74175_1_p10, _74175_1_p11, _74175_2_p5,
       _74175_2_p9, _74175_2_p10, _74175_2_p11, _74175_3_p5, _74175_4_p5, _74191_1_p1, _74191_1_p2,
       _74191_1_p3, _74191_1_p7, _74191_1_p11, _74191_1_p12, _74191_1_p13, _74191_2_p1, _74191_2_p2,
       _74191_2_p3, _74191_3_p11, _74191_3_p12, _74191_3_p13, _744017_1_p5, _744017_1_p6, _744017_1_p7,
       and_1_out, and_2_out, delay_1_out, delay_2_out, driver_2_out, not_9_out, not_10_out, or_1_out;
  wire [2:0] _74191_2_p11, _74191_4_p11, driver_4_out;
  wire [7:0] driverinvsel_3_out, not_7_out, not_17_out;

  // _74191 _74191_1: pin names not known; wires that end beside it: _74191_1_p1, _74191_1_p2, _74191_1_p3, 1'b0, 1'b1, 1'b0, _74191_1_p7, 1'b0, 1'b0, clk, _74191_1_p11, _74191_1_p12, _74191_1_p13
  Delay #(.delayTime(2)) delay_1 (.in(not_9_out), .out(delay_1_out));
  assign _74191_1_p7 = delay_1_out ? not_9_out : 1'bz;  // Driver driver_1
  assign _74191_1_p7 = ~delay_1_out ? 1'b1 : 1'bz;  // DriverInvSel driverinvsel_1
  // _74175 _74175_1: pin names not known; wires that end beside it: _74191_1_p11, _74191_1_p12, _74191_1_p13, 1'b0, _74175_1_p5, 1'b1, 1'b1, 1'b0, _74175_1_p9, _74175_1_p10, _74175_1_p11
  // _74138 _74138_1: pin names not known; wires that end beside it: 1'b1, 1'b0, 1'b1, 1'b0, 1'b0, _74191_1_p11, _74191_1_p12, _74191_1_p13, _74138_1_p9, _74138_1_p10, _74138_1_p11, _74138_1_p12, _74138_1_p13, _74138_1_p14, _74138_1_p15, _74138_1_p16
  // _74191 _74191_2: pin names not known; wires that end beside it: _74191_2_p1, _74191_2_p2, _74191_2_p3, 1'b0, 1'b1, 1'b0, _74191_1_p7, 1'b0, 1'b0, clk, _74191_2_p11[0], _74191_2_p11[1], _74191_2_p11[2]
  not not_1 (not_7_out[0], _74138_1_p9);
  not not_2 (not_7_out[1], _74138_1_p10);
  not not_3 (not_7_out[2], _74138_1_p11);
  not not_4 (not_7_out[3], _74138_1_p12);
  not not_5 (not_7_out[4], _74138_1_p13);
  not not_6 (not_7_out[5], _74138_1_p14);
  not not_7 (not_7_out[6], _74138_1_p15);
  not not_8 (not_7_out[7], _74138_1_p16);
  or or_1 (or_1_out, _74175_1_p5, _74175_3_p5);
  and and_1 (and_1_out, _74191_2_p11[0], _74191_2_p11[1], _74191_2_p11[2]);
  // _74175 _74175_2: pin names not known; wires that end beside it: _74191_2_p11[0], _74191_2_p11[1], _74191_2_p11[2], 1'b0, _74175_2_p5, 1'b1, 1'b1, 1'b0, _74175_2_p9, _74175_2_p10, _74175_2_p11
  // _744017 _744017_1: pin names not known; wires that end beside it: 1'b1, 1'b0, 1'b0, or_1_out, _744017_1_p5, _744017_1_p6, _744017_1_p7, _744017_1_p5
  not not_9 (not_9_out, _744017_1_p7);
  not not_10 (not_10_out, _744017_1_p6);
  or or_2 (_74175_2_p5, _74138_1_p9, not_7_out[7], and_1_out);
  xor xor_1 (_74175_1_p5, _74175_2_p5, not_10_out);
  Delay #(.delayTime(2)) delay_2 (.in(not_10_out), .out(delay_2_out));
  assign driver_2_out = delay_2_out ? not_10_out : 1'bz;  // Driver driver_2
  assign driver_2_out = ~delay_2_out ? 1'b1 : 1'bz;  // DriverInvSel driverinvsel_2
  // _74191 _74191_3: pin names not known; wires that end beside it: _74175_1_p9, _74175_1_p10, _74175_1_p11, 1'b0, 1'b1, 1'b0, driver_2_out, 1'b1, 1'b0, clk, _74191_3_p11, _74191_3_p12, _74191_3_p13
  // _74138 _74138_2: pin names not known; wires that end beside it: 1'b1, 1'b0, 1'b1, 1'b0, 1'b0, _74191_3_p11, _74191_3_p12, _74191_3_p13, _74138_2_p9, _74138_2_p10, _74138_2_p11, _74138_2_p12, _74138_2_p13, _74138_2_p14, _74138_2_p15, _74138_2_p16
  // _74191 _74191_4: pin names not known; wires that end beside it: _74175_2_p9, _74175_2_p10, _74175_2_p11, 1'b0, 1'b1, 1'b0, driver_2_out, 1'b1, 1'b0, clk, _74191_4_p11[0], _74191_4_p11[1], _74191_4_p11[2]
  // _74175 _74175_3: pin names not known; wires that end beside it: _74191_3_p11, _74191_3_p12, _74191_3_p13, 1'b0, _74175_3_p5, 1'b1, 1'b1, 1'b0, _74191_1_p1, _74191_1_p2, _74191_1_p3
  not not_11 (not_17_out[0], _74138_2_p9);
  not not_12 (not_17_out[1], _74138_2_p10);
  not not_13 (not_17_out[2], _74138_2_p11);
  not not_14 (not_17_out[3], _74138_2_p12);
  not not_15 (not_17_out[4], _74138_2_p13);
  not not_16 (not_17_out[5], _74138_2_p14);
  not not_17 (not_17_out[6], _74138_2_p15);
  not not_18 (not_17_out[7], _74138_2_p16);
  and and_2 (and_2_out, _74191_4_p11[0], _74191_4_p11[1], _74191_4_p11[2]);
  // _74175 _74175_4: pin names not known; wires that end beside it: _74191_4_p11[0], _74191_4_p11[1], _74191_4_p11[2], 1'b0, _74175_4_p5, 1'b1, 1'b1, 1'b0, _74191_2_p1, _74191_2_p2, _74191_2_p3
  or or_3 (_74175_4_p5, _74138_2_p9, not_17_out[7], and_2_out);
  xor xor_2 (_74175_3_p5, _74175_4_p5, not_9_out);
  assign driverinvsel_3_out = ~not_10_out ? not_17_out : 8'bz;  // DriverInvSel driverinvsel_3
  assign driverinvsel_3_out = not_10_out ? not_7_out : 8'bz;  // Driver driver_3
  assign driver_4_out = not_9_out ? _74191_4_p11 : 3'bz;  // Driver driver_4
  assign driver_4_out = ~not_9_out ? _74191_2_p11 : 3'bz;  // DriverInvSel driverinvsel_4
  LedMatrix ledmatrix_1 (.rows(driverinvsel_3_out), .column(driver_4_out));

  // Notes on the sheet:
  //   clk: Hz: 5
endmodule
