// Digital circuit Ping_Pongv3.dig as structural Verilog
module Ping_Pongv3 (
  input  clk,
  input  clk_2
);

  wire _74138_1_p9, _74138_1_p10, _74138_1_p11, _74138_1_p12, _74138_1_p13, _74138_1_p14, _74138_1_p15,
       _74138_1_p16, _74139_1_p9, _74139_1_p10, _74139_1_p11, _74139_1_p12, _74191_1_p1, _74191_1_p2,
       _74191_1_p3, _74191_1_p8, _74191_1_p11, _74191_1_p12, _74191_1_p13, _74191_2_p7, _74191_2_p9,
       _74191_2_p11, _74191_2_p12, _74191_2_p13, _74191_3_p1, _74191_3_p2, _74191_3_p3, _74191_3_p8,
       _74191_4_p7, _74191_4_p11, _74191_4_p12, and_1_out, nor_1_out, not_11_out, not_12_out, not_13_out;
  wire [2:0] _74191_3_p13;
  wire [7:0] not_9_out;

  // _74191 _74191_1: pin names not known; wires that end beside it: _74191_1_p1, _74191_1_p2, _74191_1_p3, 1'b0, 1'b1, 1'b0, 1'b1, _74191_1_p8, 1'b0, clk, _74191_1_p11, _74191_1_p12, _74191_1_p13
  // _74191 _74191_2: pin names not known; wires that end beside it: 1'b0, 1'b0, 1'b0, 1'b0, 1'b1, 1'b0, _74191_2_p7, 1'b0, _74191_2_p9, clk_2, _74191_2_p11, _74191_2_p12, _74191_2_p13
  not not_1 (_74191_2_p7, _74191_2_p13);
  // _74175 _74175_1: pin names not known; wires that end beside it: _74191_1_p11, _74191_1_p12, _74191_1_p13, 1'b0, _74191_2_p9, 1'b1, 1'b1, 1'b0, _74191_1_p1, _74191_1_p2, _74191_1_p3
  // _74138 _74138_1: pin names not known; wires that end beside it: 1'b1, 1'b0, 1'b1, 1'b0, 1'b0, _74191_1_p11, _74191_1_p12, _74191_1_p13, _74138_1_p9, _74138_1_p10, _74138_1_p11, _74138_1_p12, _74138_1_p13, _74138_1_p14, _74138_1_p15, _74138_1_p16
  // _74191 _74191_3: pin names not known; wires that end beside it: _74191_3_p1, _74191_3_p2, _74191_3_p3, 1'b0, 1'b1, 1'b0, 1'b1, _74191_3_p8, 1'b0, clk, _74191_3_p13[0], _74191_3_p13[1], _74191_3_p13[2]
  not not_2 (not_9_out[0], _74138_1_p9);
  not not_3 (not_9_out[1], _74138_1_p10);
  not not_4 (not_9_out[2], _74138_1_p11);
  not not_5 (not_9_out[3], _74138_1_p12);
  not not_6 (not_9_out[4], _74138_1_p13);
  not not_7 (not_9_out[5], _74138_1_p14);
  not not_8 (not_9_out[6], _74138_1_p15);
  not not_9 (not_9_out[7], _74138_1_p16);
  // _74191 _74191_4: pin names not known; wires that end beside it: _74191_2_p11, _74191_2_p12, 1'b0, 1'b0, 1'b1, 1'b0, _74191_4_p7, 1'b0, 1'b0, 1'b0, _74191_4_p11, _74191_4_p12
  nor nor_1 (nor_1_out, _74191_3_p13[0], _74191_3_p13[1], _74191_3_p13[2]);
  and and_1 (and_1_out, _74191_3_p13[0], _74191_3_p13[1], _74191_3_p13[2]);
  // _74175 _74175_2: pin names not known; wires that end beside it: _74191_3_p13[0], _74191_3_p13[1], _74191_3_p13[2], 1'b0, _74191_2_p9, 1'b1, 1'b1, 1'b0, _74191_3_p1, _74191_3_p2, _74191_3_p3
  LedMatrix ledmatrix_1 (.rows(not_9_out), .column(_74191_3_p13));
  not not_10 (_74191_4_p7, _74191_2_p9);
  // _74139 _74139_1: pin names not known; wires that end beside it: _74191_4_p11, _74191_4_p12, 1'b0, 1'b0, 1'b0, 1'b1, 1'b1, 1'b0, _74139_1_p9, _74139_1_p10, _74139_1_p11, _74139_1_p12
  or or_1 (_74191_2_p9, not_9_out[0], not_9_out[7], nor_1_out, and_1_out);
  assign _74191_1_p8 = ~_74139_1_p9 ? _74139_1_p9 : 1'bz;  // DriverInvSel driverinvsel_1
  not not_11 (not_11_out, _74139_1_p9);
  not not_12 (not_12_out, _74139_1_p10);
  not not_13 (not_13_out, _74139_1_p12);
  assign _74191_3_p8 = ~_74139_1_p12 ? _74139_1_p12 : 1'bz;  // DriverInvSel driverinvsel_2
  assign _74191_3_p8 = not_11_out ? not_11_out : 1'bz;  // Driver driver_1
  assign _74191_3_p8 = not_12_out ? not_12_out : 1'bz;  // Driver driver_2
  assign _74191_1_p8 = not_12_out ? not_12_out : 1'bz;  // Driver driver_3
  assign _74191_1_p8 = not_13_out ? not_13_out : 1'bz;  // Driver driver_4
  assign _74191_1_p8 = ~_74139_1_p11 ? _74139_1_p11 : 1'bz;  // DriverInvSel driverinvsel_3
  assign _74191_3_p8 = ~_74139_1_p11 ? _74139_1_p11 : 1'bz;  // DriverInvSel driverinvsel_4

  // Notes on the sheet:
  //   clk: Hz: 5
  //   clk_2: Hz: 2147483647
endmodule
