// Digital circuit Ping_Pongv5.dig as structural Verilog
module Ping_Pongv5 (
  input  clk,
  input  clk_2
);

  wire _74139_1_pin16, _74154_1_p9, _74154_1_p10, _74154_1_p11, _74154_1_p12, _74154_1_p13, _74154_1_p14,
       _74154_1_p15, _74154_1_p16, _74154_1_p17, _74154_1_p18, _74154_1_p19, _74154_1_p20, _74154_1_p21,
       _74154_1_p22, _74154_1_p23, _74154_1_p24, _74191_1_p7, _74191_1_p11, _74191_1_p12, _74191_1_p13,
       _74191_2_p9, _74191_2_p12, _74191_2_p13, _74191_2_p14, _74191_2_p15, _74191_3_p8, _74191_4_p7,
       _74191_4_p11, _74191_4_p12, _74191_4_p17, _74191_4_p18, _74191_4_p19, _74191_4_p20, and_1_out,
       delay_1_out, nor_1_out, not_20_out, not_21_out, or_1_out, or_2_out, or_3_out;
  wire [1:0] multiplexer_1_out;
  wire [3:0] _74191_3_p14, d_ff_3_q, multiplexer_2_out;
  wire [15:0] not_16_out;

  // _74191 _74191_1: pin names not known; wires that end beside it: 1'b0, 1'b0, 1'b0, 1'b0, 1'b1, 1'b0, _74191_1_p7, 1'b0, 1'b0, clk, _74191_1_p11, _74191_1_p12, _74191_1_p13
  not not_1 (_74191_1_p7, _74191_1_p13);
  // _74191 _74191_2: pin names not known; wires that end beside it: _74191_1_p11, 1'b0, 1'b0, 1'b0, 1'b0, 1'b1, 1'b0, 1'b1, _74191_2_p9, 1'b0, _74191_1_p11, _74191_2_p12, _74191_2_p13, _74191_2_p14, _74191_2_p15
  D_FF d_ff_1 (.D(or_1_out), .C(delay_1_out), .Q(d_ff_3_q[0]));  // open: nQ
  or or_1 (or_1_out, not_16_out[15], and_1_out);
  Multiplexer #(.Selector_Bits(4), .Bits(2)) multiplexer_1 (
    .sel(d_ff_3_q), .in_0(2'b11), .in_1(2'b11), .in_2(2'b00), .in_3(2'b00), .in_4(2'b10), .in_5(2'b10),
    .in_6(2'b10), .in_7(2'b01), .in_8(2'b01), .in_9(2'b01), .in_10(2'b10), .in_11(2'b10), .in_12(2'b00),
    .in_13(2'b00), .in_14(2'b00), .in_15(2'b11), .out(multiplexer_1_out));
  D_FF d_ff_2 (.D(or_2_out), .C(delay_1_out), .Q(d_ff_3_q[1]));  // open: nQ
  or or_2 (or_2_out, nor_1_out, and_1_out);
  D_FF d_ff_3 (.D(_74191_2_p9), .C(delay_1_out), .Q(d_ff_3_q[2]));  // open: nQ
  D_FF d_ff_4 (.D(_74191_3_p8), .C(delay_1_out), .Q(d_ff_3_q[3]));  // open: nQ
  // _74154 _74154_1: pin names not known; wires that end beside it: 1'b1, 1'b0, 1'b0, 1'b0, _74191_2_p12, _74191_2_p13, _74191_2_p14, _74191_2_p15, _74154_1_p9, _74154_1_p10, _74154_1_p11, _74154_1_p12, _74154_1_p13, _74154_1_p14, _74154_1_p15, _74154_1_p16, _74154_1_p17, _74154_1_p18, _74154_1_p19, _74154_1_p20, _74154_1_p21, _74154_1_p22, _74154_1_p23, _74154_1_p24
  // _74191 _74191_3: pin names not known; wires that end beside it: 1'b0, 1'b0, 1'b0, 1'b0, 1'b1, 1'b0, 1'b1, _74191_3_p8, 1'b0, _74191_1_p12, _74191_3_p14[0], _74191_3_p14[1], _74191_3_p14[2], _74191_3_p14[3]
  not not_2 (not_16_out[0], _74154_1_p9);
  not not_3 (not_16_out[1], _74154_1_p10);
  not not_4 (not_16_out[2], _74154_1_p11);
  not not_5 (not_16_out[3], _74154_1_p12);
  not not_6 (not_16_out[4], _74154_1_p13);
  not not_7 (not_16_out[5], _74154_1_p14);
  not not_8 (not_16_out[6], _74154_1_p15);
  not not_9 (not_16_out[7], _74154_1_p16);
  not not_10 (not_16_out[8], _74154_1_p17);
  not not_11 (not_16_out[9], _74154_1_p18);
  not not_12 (not_16_out[10], _74154_1_p19);
  not not_13 (not_16_out[11], _74154_1_p20);
  not not_14 (not_16_out[12], _74154_1_p21);
  not not_15 (not_16_out[13], _74154_1_p22);
  not not_16 (not_16_out[14], _74154_1_p23);
  not not_17 (not_16_out[15], _74154_1_p24);
  Delay delay_1 (.in(or_3_out), .out(delay_1_out));
  // _74191 _74191_4: pin names not known; wires that end beside it: multiplexer_1_out[0], multiplexer_1_out[1], 1'b0, 1'b0, 1'b1, 1'b0, _74191_4_p7, 1'b0, 1'b0, 1'b0, _74191_4_p11, _74191_4_p12, _74191_4_p12, 1'b0, 1'b1, 1'b0, _74191_4_p17, _74191_4_p18, _74191_4_p19, _74191_4_p20
  nor nor_1 (nor_1_out, _74191_3_p14[0], _74191_3_p14[1], _74191_3_p14[2], _74191_3_p14[3]);
  and and_1 (and_1_out, _74191_3_p14[0], _74191_3_p14[1], _74191_3_p14[2], _74191_3_p14[3]);
  Multiplexer #(.Bits(4)) multiplexer_2 (.sel(clk_2), .in_0(_74191_3_p14), .in_1(4'b1111), .out(multiplexer_2_out));
  LedMatrix #(.colAddrBits(4), .rowDataBits(16)) ledmatrix_1 (.rows(not_16_out), .column(multiplexer_2_out));
  not not_18 (_74191_4_p7, or_3_out);
  _74139 _74139_1 (
    .pin1(_74191_4_p11), .pin2(1'b0), .pin3(1'b0), .pin4(1'b1), .pin10(and_1_out), .pin12(_74191_3_p8),
    .pin16(_74139_1_pin16));  // open: pin5, pin6, pin7, pin8, pin9, pin11, pin13, pin14, pin15
  or or_3 (or_3_out, not_16_out[0], not_16_out[15], nor_1_out, and_1_out);
  assign _74191_2_p9 = ~_74191_4_p17 ? _74191_4_p17 : 1'bz;  // DriverInvSel driverinvsel_1
  not not_19 (_74139_1_pin16, _74191_4_p17);
  not not_20 (not_20_out, _74191_4_p18);
  not not_21 (not_21_out, _74191_4_p20);
  assign _74191_3_p8 = ~_74191_4_p20 ? _74191_4_p20 : 1'bz;  // DriverInvSel driverinvsel_2
  assign _74191_3_p8 = _74139_1_pin16 ? _74139_1_pin16 : 1'bz;  // Driver driver_1
  assign _74191_3_p8 = not_20_out ? not_20_out : 1'bz;  // Driver driver_2
  assign _74191_2_p9 = not_20_out ? not_20_out : 1'bz;  // Driver driver_3
  assign _74191_2_p9 = not_21_out ? not_21_out : 1'bz;  // Driver driver_4
  assign _74191_2_p9 = ~_74191_4_p19 ? _74191_4_p19 : 1'bz;  // DriverInvSel driverinvsel_3
  assign _74191_3_p8 = ~_74191_4_p19 ? _74191_4_p19 : 1'bz;  // DriverInvSel driverinvsel_4

  // Notes on the sheet:
  //   clk: Hz: 30
  //   clk_2: Hz: 276447231
endmodule
