// Digital circuit Ping_Pongv6.dig as structural Verilog
module Ping_Pongv6 (
  input  clk,
  input  clk_2,
  input  clk_3,
  input  in_4,
  input  clk_4
);

  wire _74154_1_p9, _74154_1_p10, _74154_1_p11, _74154_1_p12, _74154_1_p13, _74154_1_p14, _74154_1_p15,
       _74154_1_p16, _74154_1_p17, _74154_1_p18, _74154_1_p19, _74154_1_p20, _74154_1_p21, _74154_1_p22,
       _74154_1_p23, _74154_1_p24, _74191_1_p11, _74191_1_p12, _74191_1_p13, _74191_1_p14, _74191_2_p7,
       _74191_2_p8, _74191_2_p9, _74191_2_p10, _74191_3_p7, _74191_3_p11, _74191_3_p12, _74191_3_p13,
       _74191_4_p11, _74191_4_p12, _74191_4_p13, _74191_4_p14, _74191_6_p8, _74191_6_p10, _74191_7_p12,
       _74191_7_p13, and_1_out, and_2_out, and_3_out, button_1_out, button_2_out, delay_1_out, nor_1_out,
       not_17_out, or_1_out, or_2_out, or_5_out;
  wire [1:0] _74191_4_p8;
  wire [3:0] _74191_5_p15, _74191_6_p11, d_ff_3_q, multiplexer_2_out;
  wire [14:1] not_16_out;

  // _74191 _74191_1: pin names not known; wires that end beside it: 1'b0, 1'b0, 1'b0, 1'b0, 1'b1, 1'b0, 1'b1, 1'b0, 1'b0, clk_3, _74191_1_p11, _74191_1_p12, _74191_1_p13, _74191_1_p14
  // _74191 _74191_2: pin names not known; wires that end beside it: 1'b1, 1'b0, 1'b1, 1'b0, 1'b0, clk_4, _74191_2_p7, _74191_2_p8, _74191_2_p9, _74191_2_p10
  // _74191 _74191_3: pin names not known; wires that end beside it: 1'b0, 1'b0, 1'b0, 1'b0, 1'b1, 1'b0, _74191_3_p7, 1'b0, 1'b0, clk, _74191_3_p11, _74191_3_p12, _74191_3_p13
  not not_1 (_74191_3_p7, _74191_3_p11);
  and and_1 (and_1_out, _74191_3_p12, in_4);
  // _74191 _74191_4: pin names not known; wires that end beside it: _74191_1_p11, _74191_1_p12, _74191_1_p13, _74191_1_p14, 1'b1, 1'b0, in_4, _74191_4_p8[0], 1'b0, and_1_out, _74191_4_p11, _74191_4_p12, _74191_4_p13, _74191_4_p14
  and and_2 (and_2_out, in_4, _74191_3_p13);
  D_FF d_ff_1 (.D(or_1_out), .C(delay_1_out), .Q(d_ff_3_q[0]));  // open: nQ
  or or_1 (or_1_out, not_17_out, and_3_out);
  Multiplexer #(.Selector_Bits(4), .Bits(2)) multiplexer_1 (
    .sel(d_ff_3_q), .in_0(2'b01), .in_1(2'b01), .in_2(2'b10), .in_3(2'b10), .in_4(2'b00), .in_5(2'b00),
    .in_6(2'b11), .in_7(2'b11), .in_8(2'b11), .in_9(2'b11), .in_10(2'b00), .in_11(2'b00), .in_12(2'b10),
    .in_13(2'b10), .in_14(2'b01), .in_15(2'b01), .out(_74191_4_p8));
  D_FF d_ff_2 (.D(or_2_out), .C(delay_1_out), .Q(d_ff_3_q[1]));  // open: nQ
  or or_2 (or_2_out, nor_1_out, and_3_out);
  D_FF d_ff_3 (.D(_74191_4_p8[0]), .C(delay_1_out), .Q(d_ff_3_q[2]));  // open: nQ
  D_FF d_ff_4 (.D(_74191_4_p8[1]), .C(delay_1_out), .Q(d_ff_3_q[3]));  // open: nQ
  // _74154 _74154_1: pin names not known; wires that end beside it: 1'b1, 1'b0, 1'b0, 1'b0, _74191_4_p11, _74191_4_p12, _74191_4_p13, _74191_4_p14, _74154_1_p9, _74154_1_p10, _74154_1_p11, _74154_1_p12, _74154_1_p13, _74154_1_p14, _74154_1_p15, _74154_1_p16, _74154_1_p17, _74154_1_p18, _74154_1_p19, _74154_1_p20, _74154_1_p21, _74154_1_p22, _74154_1_p23, _74154_1_p24
  // _74191 _74191_5: pin names not known; wires that end beside it: _74191_2_p7, _74191_2_p8, _74191_2_p9, _74191_2_p10, 1'b1, 1'b0, 1'b0, in_4, _74191_4_p8[1], 1'b0, and_2_out, _74191_5_p15[0], _74191_5_p15[1], _74191_5_p15[2], _74191_5_p15[3], clk_2
  // _74191 _74191_6: pin names not known; wires that end beside it: 1'b1, 1'b1, 1'b1, 1'b1, 1'b1, 1'b0, 1'b1, _74191_6_p8, 1'b0, _74191_6_p10, _74191_6_p11[0], _74191_6_p11[1], _74191_6_p11[2], _74191_6_p11[3]
  Delay delay_1 (.in(or_5_out), .out(delay_1_out));
  // Not not_2 has open pins: in=_74154_1_p9, out=open
  not not_3 (not_16_out[1], _74154_1_p10);
  not not_4 (not_16_out[2], _74154_1_p11);
  not not_5 (not_16_out[3], _74154_1_p12);
  not not_6 (not_16_out[4], _74154_1_p13);
  not not_7 (not_16_out[5], _74154_1_p14);
  not not_8 (not_16_out[6], _74154_1_p15);
  not not_9 (not_16_out[7], _74154_1_p16);
  not not_10 (not_16_out[8], _74154_1_p17);
  not not_11 (not_16_out[9], _74154_1_p18);
  not not_12 (not_16_out[10], _74154_1_p19);
  not not_13 (not_16_out[11], _74154_1_p20);
  not not_14 (not_16_out[12], _74154_1_p21);
  not not_15 (not_16_out[13], _74154_1_p22);
  not not_16 (not_16_out[14], _74154_1_p23);
  not not_17 (not_17_out, _74154_1_p24);
  Button button_1 (.out(button_1_out));
  Button button_2 (.out(button_2_out));
  or or_3 (_74191_6_p8, button_2_out, ~button_1_out);  // Or
  or or_4 (_74191_6_p10, button_2_out, button_1_out);
  nor nor_1 (nor_1_out, _74191_5_p15[0], _74191_5_p15[1], _74191_5_p15[2], _74191_5_p15[3]);
  and and_3 (and_3_out, _74191_5_p15[0], _74191_5_p15[1], _74191_5_p15[2], _74191_5_p15[3]);
  Multiplexer #(.Bits(4)) multiplexer_2 (
    .sel(clk_2), .in_0(_74191_5_p15), .in_1(_74191_6_p11), .out(multiplexer_2_out));
  LedMatrix #(.colAddrBits(4), .rowDataBits(16)) ledmatrix_1 (
    .rows({clk_2, not_16_out, clk_2}), .column(multiplexer_2_out));
  or or_5 (or_5_out, not_16_out[1], not_16_out[14], nor_1_out, and_3_out);
  // _74191 _74191_7: pin names not known; wires that end beside it: clk_2, 1'b0, 1'b0, 1'b0, 1'b0, 1'b1, 1'b0, 1'b1, 1'b0, 1'b0, or_5_out, _74191_7_p12, _74191_7_p13

  // Notes on the sheet:
  //   clk: Hz: 20
  //   clk_2: Hz: 276447231
  //   clk_3: Hz: 5000
  //   clk_4: Hz: 50000
endmodule
